// Logisim project Template.circ as structural Verilog: 3 circuits, main circuit main
module main (
  output [14:0] out_1,
  output [15:0] out_2
);

  wire clk;
  wire [0:0] register_1_q;
  wire [15:0] adder_1_out;

  // Text text_1: pin names not known
  // Text text_2: pin names not known
  // Text text_3: pin names not known
  // Text text_4: pin names not known
  // Text text_5: pin names not known
  Clock #(.highDuration(4), .lowDuration(4)) u_clk (.out(clk));
  Clock sysclk ();  // open: out
  Register #(.width(16)) register_1 (.D(adder_1_out), .clk(clk), .Q({out_1, register_1_q[0]}));  // open: en, clr
  Adder #(.width(16)) adder_1 (.a({out_1, register_1_q[0]}), .b(16'h2), .out(adder_1_out));  // open: cin, cout
  ROM #(.addrWidth(15), .dataWidth(16)) rom_1 (.addr(out_1), .data(out_2));

  // Notes on the sheet:
  //   LABO ARO 2 - FETCH
  //   HEIG-VD / Institut REDS
  //   Date : 25.02.2014
  //   Ne pas modifier les noms des clocks
  //   contents of rom_1 (hex, n*v repeats v):
  //   202a 2101 2202 188b
endmodule

module FETCH (
);

  // Text text_1: pin names not known
  // Text text_2: pin names not known
  // Text text_3: pin names not known
  // Text text_4: pin names not known
  // Text text_5: pin names not known
  D_Flip_Flop d_ff_1 ();  // open: clk, D, Q, Qn, preset, reset
endmodule

module PC_4BITS (
  input  [3:0] in_1,
  output [3:0] out_2
);

  wire CLK;

  // Text text_1: pin names not known
  // Text text_2: pin names not known
  // Text text_3: pin names not known
  // Text text_4: pin names not known
  // Text text_5: pin names not known
  Clock u_CLK (.out(CLK));
  D_Flip_Flop d_ff_1 (.D(in_1[0]), .clk(CLK), .Q(out_2[0]));  // open: Qn, preset, reset
  D_Flip_Flop d_ff_2 (.D(in_1[1]), .clk(CLK), .Q(out_2[1]));  // open: Qn, preset, reset
  D_Flip_Flop d_ff_3 (.D(in_1[2]), .clk(CLK), .Q(out_2[2]));  // open: Qn, preset, reset
  D_Flip_Flop d_ff_4 (.D(in_1[3]), .clk(CLK), .Q(out_2[3]));  // open: Qn, preset, reset
endmodule
